// Logisim project sutra_1.circ as structural Verilog
module main (
  input  in_1,
  output [9:0] IR_CONTENTS,
  output [36:0] FLAGS_CONTENT
);

  wire ACCU_out, ALUFSET_out, and10_1_o, bcd_to_7_segment_decoder_8_p1, CARRY_out, CLEARISR_out, clock_1_out,
       controlled_buffer_1_out, controlled_buffer_3_out, COPY_out, HALT_o, JUMP_out, LOADIL_out, LOADIU_out,
       MACHINE_CYCLE_o, MACHINE_CYCLE_oc, nand_1_out, nand_2_out, nand_3_out, nand_4_out, nand_5_out,
       nand_6_out, nand_7_out, nand_8_out, nand_9_out, nand_11_out, nand_12_out, nand_13_out, nand_14_out,
       nand_15_out, nand_16_out, nand_17_out, nand_18_out, nand_19_out, nand_20_out, nand_21_out,
       nand_22_out, nand_23_out, nand_24_out, nand_25_out, nand_26_out, nand_28_out, nand_29_out,
       nand_30_out, nand_31_out, nand_32_out, nand_33_out, nand_34_out, nand_35_out, nand_36_out,
       nand_37_out, nand_38_out, nand_39_out, nand_40_out, nand_41_out, nand_42_out, nand_43_out,
       nand_45_out, nand_46_out, nand_47_out, nand_48_out, nand_49_out, nand_50_out, nand_51_out,
       nand_52_out, nand_53_out, nand_54_out, nand_55_out, nand_56_out, nand_57_out, nand_58_out,
       nand_59_out, nand_60_out, nand_61_out, nand_62_out, nand_63_out, nand_64_out, nand_65_out,
       nand_66_out, nand_67_out, nand_68_out, nand_70_out, nand_71_out, NEGATIVE_out, or3_1_o, or4_1_o,
       or4_2_o, or4_3_o, or5_1_o, or10_1_o, ZERO_out;
  wire [0:0] nand_10_out;
  wire [2:0] ALU_RESULT_FLAGS_o, INSTRUCTION_DATA_OUT_o_2, nand_44_out;
  wire [3:0] IMR_o, ISR_o, LOAD_out, nand_73_out;
  wire [4:1] ALUEVAL_out;
  wire [6:0] aluflagsregister_1_o, INSTRUCTION_DATA_OUT_o;
  wire [9:0] alu_1_o, ALU_RESULT_o, ALUFSET_FLAGS_o, B_o, binary_to_bcd_converter_1_p1, buffer10_4_o, C_o,
       COPY_RS_o, D_o, LOADIL_DATA_o, LOADIL_U_R_o, SP_o;
  wire [9:2] buffer10_1_o, COPY_R_OR_ALUSTOREF_R_OR_ALUSTORER_R_OR_LOAD_o;
  wire [9:3] ALUEVAL_RS_OR_STORE_OUT_ALUFSET_REGISTER_o, undriven_6;
  wire [19:0] buffer20_1_o, MAR_o, PC_o;
  wire [26:6] undriven, undriven_4;
  wire [34:7] undriven_2, undriven_3, undriven_5;
  wire [36:0] controldestination_1_o;

  Or4 or4_1 (.I(LOAD_out), .O(or4_1_o));
  Buffer10 LOADIL_U_R (.I(IR_CONTENTS), .E(nand_10_out[0]), .O(LOADIL_U_R_o));
  Buffer10 COPY_R_OR_ALUSTOREF_R_OR_ALUSTORER_R_OR_LOAD (
    .I(IR_CONTENTS), .E(or4_1_o), .O({COPY_R_OR_ALUSTOREF_R_OR_ALUSTORER_R_OR_LOAD_o, LOADIL_U_R_o[6:5]}));
  Or4 or4_2 (.I({LOAD_out[3:1], nand_10_out[0]}), .O(or4_2_o));
  assign controlled_buffer_1_out = nand_10_out[0] ? LOADIL_U_R_o[7] : 1'bz;  // Controlled_Buffer controlled_buffer_1
  assign COPY_R_OR_ALUSTOREF_R_OR_ALUSTORER_R_OR_LOAD_o[2] = nand_10_out[0] ? 1'b0 : 1'bz;  // Controlled_Buffer controlled_buffer_2
  assign controlled_buffer_3_out = nand_10_out[0] ? LOADIL_U_R_o[8] : 1'bz;  // Controlled_Buffer controlled_buffer_3
  assign controlled_buffer_1_out = LOAD_out[1] ? 1'b1 : 1'bz;  // Controlled_Buffer controlled_buffer_4
  assign controlled_buffer_3_out = LOAD_out[1] ? 1'b1 : 1'bz;  // Controlled_Buffer controlled_buffer_5
  assign controlled_buffer_1_out = LOAD_out[2] ? 1'b1 : 1'bz;  // Controlled_Buffer controlled_buffer_6
  assign controlled_buffer_3_out = LOAD_out[2] ? 1'b1 : 1'bz;  // Controlled_Buffer controlled_buffer_7
  assign controlled_buffer_1_out = LOAD_out[3] ? 1'b1 : 1'bz;  // Controlled_Buffer controlled_buffer_8
  assign controlled_buffer_3_out = LOAD_out[3] ? 1'b1 : 1'bz;  // Controlled_Buffer controlled_buffer_9
  Or3 or3_1 (.I(ALUEVAL_out[3:1]), .O(or3_1_o));
  ControlDestination controldestination_1 (
    .OUTPUT_ENABLE(or4_2_o), .UPPER(controlled_buffer_1_out), .LOWER(controlled_buffer_3_out),
    .S({COPY_R_OR_ALUSTOREF_R_OR_ALUSTORER_R_OR_LOAD_o[2], LOADIL_U_R_o[6:5]}), .O(controldestination_1_o));
  Clock clock_1 (.out(clock_1_out));
  nand nand_1 (nand_1_out, nand_13_out, clock_1_out);
  Buffer10 COPY_RS (.I(IR_CONTENTS), .E(LOAD_out[1]), .O(COPY_RS_o));
  Buffer10 ALUEVAL_RS_OR_STORE_OUT_ALUFSET_REGISTER (
    .I(IR_CONTENTS), .E(or3_1_o), .O({ALUEVAL_RS_OR_STORE_OUT_ALUFSET_REGISTER_o, COPY_RS_o[5:3]}));
  nand nand_2 (nand_2_out, nand_1_out, nand_1_out);
  Or5 or5_1 (.I({ALUEVAL_out, LOAD_out[1]}), .O(or5_1_o));
  Buffer10 buffer10_1 (.I(IR_CONTENTS), .E(ALUEVAL_out[3]), .O({buffer10_1_o, COPY_RS_o[4:3]}));
  nand nand_3 (nand_3_out, MACHINE_CYCLE_oc, nand_2_out);
  assign COPY_RS_o[5] = ALUEVAL_out[3] ? 1'b0 : 1'bz;  // Controlled_Buffer controlled_buffer_10
  nand nand_4 (nand_4_out, nand_3_out, nand_3_out);
  Buffer10 INSTRUCTION_DATA_OUT (
    .I(LOADIL_DATA_o), .E(nand_4_out), .O({INSTRUCTION_DATA_OUT_o_2, INSTRUCTION_DATA_OUT_o}));
  ControlSource controlsource_1 (.OUTPUT_ENABLE(or5_1_o), .S(COPY_RS_o[5:3]), .O(controldestination_1_o));
  Buffer10 ALUFSET_FLAGS (.I({3'b000, IR_CONTENTS[9:3]}), .E(ALUFSET_out), .O(ALUFSET_FLAGS_o));
  JKFlipFlop MACHINE_CYCLE (
    .SB(in_1), .J(1'b1), .CLK(nand_2_out), .K(1'b1), .O(MACHINE_CYCLE_o), .OC(MACHINE_CYCLE_oc));
  NormalRegister IR (
    .CLK(nand_2_out), .LL(nand_26_out), .LH(nand_26_out), .SB(in_1),
    .I({INSTRUCTION_DATA_OUT_o_2, INSTRUCTION_DATA_OUT_o}), .O(IR_CONTENTS));
  Buffer37 FETCH (.I(37'h50000000), .E(nand_26_out), .O(FLAGS_CONTENT));
  nand nand_5 (nand_5_out, IR_CONTENTS[9], IR_CONTENTS[9]);
  nand nand_6 (nand_6_out, IR_CONTENTS[8], IR_CONTENTS[8]);
  nand nand_7 (nand_7_out, IR_CONTENTS[7], IR_CONTENTS[7]);
  Buffer10 IR_OUT (.I(IR_CONTENTS), .E(FLAGS_CONTENT[36]), .O({INSTRUCTION_DATA_OUT_o_2, INSTRUCTION_DATA_OUT_o}));
  nand nand_8 (nand_8_out, nand_5_out, IR_CONTENTS[8]);
  NormalRegister B (
    .CLK(nand_2_out), .LL(FLAGS_CONTENT[11]), .LH(FLAGS_CONTENT[12]), .SB(in_1),
    .I({INSTRUCTION_DATA_OUT_o_2, INSTRUCTION_DATA_OUT_o}), .O(B_o));
  nand nand_9 (nand_9_out, nand_8_out, nand_8_out);
  nand nand_10 (nand_10_out[0], nand_11_out, nand_19_out);
  _7_Segment_Display u_7_segment_display_1 ();  // open: g, f, a, b, e, d, c, dp
  // BCD_to_7_Segment_decoder bcd_to_7_segment_decoder_1: pin names not known
  // Binary_to_BCD_converter #(.binvalue(10)) binary_to_bcd_converter_1: pin names not known; wires that end beside it: binary_to_bcd_converter_1_p1
  _7_Segment_Display u_7_segment_display_2 ();  // open: g, f, a, b, e, d, c, dp
  // BCD_to_7_Segment_decoder bcd_to_7_segment_decoder_2: pin names not known
  // Binary_to_BCD_converter #(.binvalue(10)) binary_to_bcd_converter_2: pin names not known; wires that end beside it: B_o
  nand nand_11 (nand_11_out, nand_7_out, nand_9_out);
  nand LOADIL (LOADIL_out, nand_11_out, nand_11_out);
  Clock clock_2 ();  // open: out
  _7_Segment_Display u_7_segment_display_3 ();  // open: g, f, a, b, e, d, c, dp
  // BCD_to_7_Segment_decoder bcd_to_7_segment_decoder_3: pin names not known
  _7_Segment_Display u_7_segment_display_4 ();  // open: g, f, a, b, e, d, c, dp
  _7_Segment_Display u_7_segment_display_5 ();  // open: g, f, a, b, e, d, c, dp
  // BCD_to_7_Segment_decoder bcd_to_7_segment_decoder_4: pin names not known
  // BCD_to_7_Segment_decoder bcd_to_7_segment_decoder_5: pin names not known
  _7_Segment_Display u_7_segment_display_6 ();  // open: g, f, a, b, e, d, c, dp
  // BCD_to_7_Segment_decoder bcd_to_7_segment_decoder_6: pin names not known
  Buffer10 buffer10_2 (.I(B_o), .E(FLAGS_CONTENT[13]), .O({INSTRUCTION_DATA_OUT_o_2, INSTRUCTION_DATA_OUT_o}));
  _7_Segment_Display u_7_segment_display_7 ();  // open: g, f, a, b, e, d, c, dp
  // BCD_to_7_Segment_decoder bcd_to_7_segment_decoder_7: pin names not known
  Buffer37 INSTRUCTION_FLAGS_OUT (.I(controldestination_1_o), .E(nand_4_out), .O(FLAGS_CONTENT));
  Buffer37 ALUFSET_O (.I(37'h20), .E(ALUFSET_out), .O(controldestination_1_o));
  _7_Segment_Display u_7_segment_display_8 ();  // open: g, f, a, b, e, d, c, dp
  // BCD_to_7_Segment_decoder bcd_to_7_segment_decoder_8: pin names not known; wires that end beside it: bcd_to_7_segment_decoder_8_p1
  UniversalShiftRegister A (
    .CLK(nand_2_out), .LL(FLAGS_CONTENT[7]), .LH(FLAGS_CONTENT[8]), .SB(in_1), .S1(FLAGS_CONTENT[9]),
    .S2(FLAGS_CONTENT[10]), .I({INSTRUCTION_DATA_OUT_o_2, INSTRUCTION_DATA_OUT_o}),
    .O(binary_to_bcd_converter_1_p1));
  Buffer10 LOADIL_DATA (.I({{5{1'b0}}, IR_CONTENTS[4:0]}), .E(LOADIL_out), .O(LOADIL_DATA_o));
  Buffer10 LOADIU_DATA (.I({IR_CONTENTS[4:0], {5{1'b0}}}), .E(LOADIU_out), .O(LOADIL_DATA_o));
  Clock clock_3 (.out(bcd_to_7_segment_decoder_8_p1));
  And10 HALT (.I(IR_CONTENTS), .O(HALT_o));
  And10 and10_1 (.I(IR_CONTENTS), .O(and10_1_o));
  nand nand_12 (nand_12_out, IR_CONTENTS[7], nand_9_out);
  Buffer10 buffer10_3 (
    .I(binary_to_bcd_converter_1_p1), .E(FLAGS_CONTENT[6]),
    .O({INSTRUCTION_DATA_OUT_o_2, INSTRUCTION_DATA_OUT_o}));
  NormalRegister C (
    .CLK(nand_2_out), .LL(FLAGS_CONTENT[14]), .LH(FLAGS_CONTENT[15]), .SB(in_1),
    .I({INSTRUCTION_DATA_OUT_o_2, INSTRUCTION_DATA_OUT_o}), .O(C_o));
  nand nand_13 (nand_13_out, HALT_o, HALT_o);
  nand ALUFSET (ALUFSET_out, nand_12_out, nand_12_out);
  nand nand_14 (nand_14_out, IR_CONTENTS[8], IR_CONTENTS[8]);
  nand nand_15 (nand_15_out, nand_5_out, nand_6_out);
  nand nand_16 (nand_16_out, nand_18_out, nand_7_out);
  nand nand_17 (nand_17_out, nand_14_out, IR_CONTENTS[9]);
  _7_Segment_Display u_7_segment_display_9 ();  // open: g, f, a, b, e, d, c, dp
  // BCD_to_7_Segment_decoder bcd_to_7_segment_decoder_9: pin names not known
  // Binary_to_BCD_converter #(.binvalue(10)) binary_to_bcd_converter_3: pin names not known; wires that end beside it: C_o
  Buffer37 buffer37_1 (.I({37{1'b0}}), .E(and10_1_o), .O(controldestination_1_o));
  nand nand_18 (nand_18_out, nand_15_out, nand_15_out);
  nand COPY (COPY_out, nand_16_out, nand_16_out);
  nand nand_19 (nand_19_out, nand_18_out, IR_CONTENTS[7]);
  nand LOADIU (LOADIU_out, nand_19_out, nand_19_out);
  nand nand_20 (nand_20_out, IR_CONTENTS[7], IR_CONTENTS[7]);
  nand nand_21 (nand_21_out, nand_17_out, nand_17_out);
  Buffer10 buffer10_4 (.I({INSTRUCTION_DATA_OUT_o_2, INSTRUCTION_DATA_OUT_o}), .E(FLAGS_CONTENT[4]), .O(buffer10_4_o));
  _7_Segment_Display u_7_segment_display_10 ();  // open: g, f, a, b, e, d, c, dp
  _7_Segment_Display u_7_segment_display_11 ();  // open: g, f, a, b, e, d, c, dp
  // BCD_to_7_Segment_decoder bcd_to_7_segment_decoder_10: pin names not known
  // BCD_to_7_Segment_decoder bcd_to_7_segment_decoder_11: pin names not known
  nand nand_22 (nand_22_out, nand_13_out, MACHINE_CYCLE_o);
  nand nand_23 (nand_23_out, COPY_out, IR_CONTENTS[6]);
  nand nand_24 (nand_24_out, nand_20_out, nand_21_out);
  nand nand_25 (nand_25_out, nand_21_out, IR_CONTENTS[7]);
  ALUFlagsRegister aluflagsregister_1 (
    .CLK(nand_2_out), .LL(FLAGS_CONTENT[5]), .LH(FLAGS_CONTENT[5]), .SB(in_1), .I(INSTRUCTION_DATA_OUT_o),
    .O(aluflagsregister_1_o));
  Buffer10 buffer10_5 (.I(C_o), .E(FLAGS_CONTENT[16]), .O({INSTRUCTION_DATA_OUT_o_2, INSTRUCTION_DATA_OUT_o}));
  _7_Segment_Display u_7_segment_display_12 ();  // open: g, f, a, b, e, d, c, dp
  // BCD_to_7_Segment_decoder bcd_to_7_segment_decoder_12: pin names not known
  nand nand_26 (nand_26_out, nand_22_out, nand_22_out);
  nand nand_27 (LOAD_out[1], nand_23_out, nand_23_out);
  nand nand_28 (nand_28_out, IR_CONTENTS[6], IR_CONTENTS[6]);
  nand nand_29 (nand_29_out, nand_24_out, nand_24_out);
  nand nand_30 (nand_30_out, nand_25_out, nand_25_out);
  nand nand_31 (nand_31_out, nand_28_out, nand_29_out);
  nand nand_32 (nand_32_out, nand_29_out, IR_CONTENTS[6]);
  nand nand_33 (nand_33_out, nand_28_out, nand_30_out);
  nand nand_34 (nand_34_out, IR_CONTENTS[5], IR_CONTENTS[5]);
  nand nand_35 (nand_35_out, nand_31_out, nand_31_out);
  nand nand_36 (nand_36_out, nand_32_out, nand_32_out);
  nand nand_37 (nand_37_out, nand_33_out, nand_33_out);
  ALU alu_1 (
    .A(binary_to_bcd_converter_1_p1), .B(buffer10_4_o), .AZ(aluflagsregister_1_o[0]),
    .AC(aluflagsregister_1_o[1]), .BZ(aluflagsregister_1_o[2]), .BC(aluflagsregister_1_o[3]),
    .Cin(aluflagsregister_1_o[4]), .N(aluflagsregister_1_o[5]), .OC(aluflagsregister_1_o[6]),
    .Cout(nand_44_out[2]), .O(alu_1_o));
  nand nand_38 (nand_38_out, nand_34_out, nand_35_out);
  nand nand_39 (nand_39_out, nand_38_out, nand_38_out);
  nand nand_40 (nand_40_out, nand_35_out, IR_CONTENTS[5]);
  nand nand_41 (nand_41_out, nand_34_out, nand_36_out);
  nand nand_42 (nand_42_out, nand_36_out, IR_CONTENTS[5]);
  nand nand_43 (nand_43_out, nand_34_out, nand_37_out);
  nand nand_44 (nand_44_out[0], or10_1_o, or10_1_o);
  NormalRegister D (
    .CLK(nand_2_out), .LL(FLAGS_CONTENT[17]), .LH(FLAGS_CONTENT[18]), .SB(in_1),
    .I({INSTRUCTION_DATA_OUT_o_2, INSTRUCTION_DATA_OUT_o}), .O(D_o));
  nand nand_45 (nand_45_out, IR_CONTENTS[4], IR_CONTENTS[4]);
  nand nand_46 (nand_46_out, nand_40_out, nand_40_out);
  nand nand_47 (nand_47_out, nand_41_out, nand_41_out);
  nand nand_48 (nand_48_out, nand_42_out, nand_42_out);
  nand nand_49 (nand_49_out, nand_43_out, nand_43_out);
  SyncCounter PC (.SB(in_1), .CLK(nand_2_out), .ENABLE(nand_26_out), .L(FLAGS_CONTENT[27]), .I(buffer20_1_o), .O(PC_o));
  NormalRegister20 MAR (
    .CLK(nand_2_out), .LLL(FLAGS_CONTENT[31]), .LLH(FLAGS_CONTENT[32]), .LHL(FLAGS_CONTENT[33]),
    .LHH(FLAGS_CONTENT[34]), .SB(in_1), .IL({INSTRUCTION_DATA_OUT_o_2, INSTRUCTION_DATA_OUT_o}),
    .IH({INSTRUCTION_DATA_OUT_o_2, INSTRUCTION_DATA_OUT_o}), .O(MAR_o));
  nand nand_50 (nand_50_out, nand_45_out, nand_39_out);
  nand ALUEVAL (ALUEVAL_out[1], nand_50_out, nand_50_out);
  nand nand_51 (nand_51_out, nand_39_out, IR_CONTENTS[4]);
  nand ALUSTOREF (LOAD_out[2], nand_51_out, nand_51_out);
  nand nand_52 (nand_52_out, nand_45_out, nand_46_out);
  nand ALUTSTORER (LOAD_out[3], nand_52_out, nand_52_out);
  nand nand_53 (nand_53_out, nand_46_out, IR_CONTENTS[4]);
  nand nand_54 (nand_54_out, nand_45_out, nand_47_out);
  nand nand_55 (nand_55_out, nand_47_out, IR_CONTENTS[4]);
  nand nand_56 (nand_56_out, nand_48_out, nand_45_out);
  nand nand_57 (nand_57_out, IR_CONTENTS[4], nand_48_out);
  nand nand_58 (nand_58_out, nand_45_out, nand_49_out);
  nand nand_59 (nand_59_out, nand_49_out, IR_CONTENTS[4]);
  nand STORE (ALUEVAL_out[2], nand_53_out, nand_53_out);
  nand LOAD (LOAD_out[0], nand_54_out, nand_54_out);
  nand ACCU (ACCU_out, nand_55_out, nand_55_out);
  nand JUMP (JUMP_out, nand_56_out, nand_56_out);
  nand OUTT (ALUEVAL_out[3], nand_57_out, nand_57_out);
  nand CLEARISR (CLEARISR_out, nand_58_out, nand_58_out);
  nand ALUFSET_REGISTER (ALUEVAL_out[4], nand_59_out, nand_59_out);
  Or10 or10_1 (.I(alu_1_o), .O(or10_1_o));
  NormalRegister ALU_RESULT (
    .CLK(nand_2_out), .LL(FLAGS_CONTENT[2]), .LH(FLAGS_CONTENT[2]), .SB(in_1), .I(alu_1_o), .O(ALU_RESULT_o));
  NormalRegister3 ALU_RESULT_FLAGS (
    .CLK(nand_2_out), .LOAD(FLAGS_CONTENT[3]), .SB(in_1), .I({nand_44_out[2], alu_1_o[9], nand_44_out[0]}),
    .O(ALU_RESULT_FLAGS_o));
  Buffer10 buffer10_6 (.I(D_o), .E(FLAGS_CONTENT[19]), .O({INSTRUCTION_DATA_OUT_o_2, INSTRUCTION_DATA_OUT_o}));
  _7_Segment_Display u_7_segment_display_13 ();  // open: g, f, a, b, e, d, c, dp
  // BCD_to_7_Segment_decoder bcd_to_7_segment_decoder_13: pin names not known
  Buffer20 buffer20_1 (.I(PC_o), .E(FLAGS_CONTENT[28]), .O(buffer20_1_o));
  Buffer20 buffer20_2 (.I(MAR_o), .E(FLAGS_CONTENT[35]), .O(buffer20_1_o));
  _7_Segment_Display u_7_segment_display_14 ();  // open: g, f, a, b, e, d, c, dp
  // BCD_to_7_Segment_decoder bcd_to_7_segment_decoder_14: pin names not known
  // Binary_to_BCD_converter #(.binvalue(10)) binary_to_bcd_converter_4: pin names not known; wires that end beside it: D_o
  RAM #(.addrWidth(20), .dataWidth(10), .databus("bidir"), .enables("line"), .trigger("high"), .\type ("nonvolatile")) ram_1 (
    .addr(buffer20_1_o), .we(FLAGS_CONTENT[29]), .oe(FLAGS_CONTENT[30]), .clk(nand_2_out),
    .data({INSTRUCTION_DATA_OUT_o_2, INSTRUCTION_DATA_OUT_o}));
  _7_Segment_Display u_7_segment_display_15 ();  // open: g, f, a, b, e, d, c, dp
  // BCD_to_7_Segment_decoder bcd_to_7_segment_decoder_15: pin names not known
  NormalRegister SP (
    .CLK(nand_2_out), .LL(FLAGS_CONTENT[24]), .LH(FLAGS_CONTENT[25]), .SB(in_1),
    .I({INSTRUCTION_DATA_OUT_o_2, INSTRUCTION_DATA_OUT_o}), .O(SP_o));
  Buffer37 buffer37_2 (
    .I({{10{1'b0}}, undriven[26], 2'b00, undriven[23:22], 2'b00, undriven[19], 2'b00, undriven[16], 2'b00, undriven[13], {6{1'b0}}, undriven[6], 6'b011100}),
    .E(ALUEVAL_out[1]), .O(controldestination_1_o));
  Buffer37 buffer37_3 (
    .I({2'b00, undriven_2[34:31], {5{1'b0}}, undriven_2[25:24], 2'b00, undriven_2[21], 2'b00, undriven_2[18:17], 1'b0, undriven_2[15:14], 1'b0, undriven_2[12:11], 1'b0, undriven_2[9:7], 7'b0000010}),
    .E(LOAD_out[2]), .O(controldestination_1_o));
  Buffer37 buffer37_4 (
    .I({2'b00, undriven_3[34:31], {5{1'b0}}, undriven_3[25:24], 2'b00, undriven_3[21], 2'b00, undriven_3[18:17], 1'b0, undriven_3[15:14], 1'b0, undriven_3[12:11], 1'b0, undriven_3[9:7], 7'b0000001}),
    .E(LOAD_out[3]), .O(controldestination_1_o));
  Buffer37 buffer37_5 (
    .I({10'h104, undriven_4[26], 2'b00, undriven_4[23:22], 2'b00, undriven_4[19], 2'b00, undriven_4[16], 2'b00, undriven_4[13], {6{1'b0}}, undriven_4[6], {6{1'b0}}}),
    .E(ALUEVAL_out[2]), .O(controldestination_1_o));
  Buffer37 buffer37_6 (
    .I({2'b01, undriven_5[34:31], 5'b10000, undriven_5[25:24], 2'b00, undriven_5[21], 2'b00, undriven_5[18:17], 1'b0, undriven_5[15:14], 1'b0, undriven_5[12:11], 1'b0, undriven_5[9:7], {7{1'b0}}}),
    .E(LOAD_out[0]), .O(controldestination_1_o));
  Buffer37 buffer37_7 (
    .I({{26{1'b0}}, IR_CONTENTS[8], IR_CONTENTS[9], {9{1'b0}}}), .E(ACCU_out), .O(controldestination_1_o));
  Buffer37 buffer37_8 (.I(37'h808000000), .E(nand_67_out), .O(controldestination_1_o));
  nand nand_60 (nand_60_out, IR_CONTENTS[0], IR_CONTENTS[0]);
  nand nand_61 (nand_61_out, IR_CONTENTS[1], IR_CONTENTS[1]);
  Buffer37 buffer37_9 (.I(37'h1000100000), .E(CLEARISR_out), .O(controldestination_1_o));
  Buffer37 buffer37_10 (.I(37'h20), .E(ALUEVAL_out[4]), .O(controldestination_1_o));
  _7_Segment_Display u_7_segment_display_16 ();  // open: g, f, a, b, e, d, c, dp
  // BCD_to_7_Segment_decoder bcd_to_7_segment_decoder_16: pin names not known
  Buffer10 buffer10_7 (.I(ALU_RESULT_o), .E(FLAGS_CONTENT[0]), .O({INSTRUCTION_DATA_OUT_o_2, INSTRUCTION_DATA_OUT_o}));
  Buffer10 buffer10_8 (
    .I({undriven_6, ALU_RESULT_FLAGS_o}), .E(FLAGS_CONTENT[1]),
    .O({INSTRUCTION_DATA_OUT_o_2, INSTRUCTION_DATA_OUT_o}));
  nand nand_62 (nand_62_out, JUMP_out, or4_3_o);
  nand nand_63 (nand_63_out, nand_60_out, nand_61_out);
  nand UNCONDITIONAL (nand_73_out[3], nand_63_out, nand_63_out);
  nand nand_64 (nand_64_out, IR_CONTENTS[1], nand_61_out);
  nand nand_65 (nand_65_out, nand_60_out, IR_CONTENTS[1]);
  nand nand_66 (nand_66_out, IR_CONTENTS[0], IR_CONTENTS[1]);
  Buffer10 buffer10_9 (.I(SP_o), .E(FLAGS_CONTENT[26]), .O({INSTRUCTION_DATA_OUT_o_2, INSTRUCTION_DATA_OUT_o}));
  nand nand_67 (nand_67_out, nand_62_out, nand_62_out);
  nand ZERO (ZERO_out, nand_64_out, nand_64_out);
  nand NEGATIVE (NEGATIVE_out, nand_65_out, nand_65_out);
  nand CARRY (CARRY_out, nand_66_out, nand_66_out);
  nand nand_68 (nand_68_out, ALU_RESULT_FLAGS_o[0], ZERO_out);
  nand nand_69 (nand_73_out[2], nand_68_out, nand_68_out);
  nand nand_70 (nand_70_out, ALU_RESULT_FLAGS_o[1], NEGATIVE_out);
  nand nand_71 (nand_71_out, ALU_RESULT_FLAGS_o[2], CARRY_out);
  nand nand_72 (nand_73_out[1], nand_70_out, nand_70_out);
  nand nand_73 (nand_73_out[0], nand_71_out, nand_71_out);
  NormalRegister4 ISR (
    .CLK(nand_2_out), .LOAD(FLAGS_CONTENT[20]), .SB(in_1), .I(INSTRUCTION_DATA_OUT_o[3:0]), .O(ISR_o));
  NormalRegister4 IMR (
    .CLK(nand_2_out), .LOAD(FLAGS_CONTENT[21]), .SB(in_1), .I(INSTRUCTION_DATA_OUT_o[3:0]), .O(IMR_o));
  Or4 or4_3 (.I(nand_73_out), .O(or4_3_o));
  Buffer4 buffer4_1 (.I(ISR_o), .E(FLAGS_CONTENT[22]), .O(INSTRUCTION_DATA_OUT_o[3:0]));
  Buffer4 buffer4_2 (.I(IMR_o), .E(FLAGS_CONTENT[23]), .O(INSTRUCTION_DATA_OUT_o[3:0]));

  // Notes on the sheet:
  //   A
  //   B
  //   C
  //   D
  //   MEMORY
endmodule

module SRLatch (
  input  S,
  input  R,
  input  SB,
  output O,
  output OC
);

  wire nand_1_out, nand_2_out;

  nand nand_1 (nand_1_out, S, S);
  nand nand_2 (nand_2_out, R, R);
  nand nand_3 (O, nand_1_out, SB, OC);
  nand nand_4 (OC, O, nand_2_out);
endmodule

module DLatch (
  input  E,
  input  D,
  input  SB,
  output O,
  output OC
);

  wire nand_1_out, nand_2_out;

  nand nand_1 (nand_1_out, E, D);
  nand nand_2 (nand_2_out, nand_1_out, E);
  nand nand_3 (O, nand_1_out, OC);
  nand nand_4 (OC, O, SB, nand_2_out);
endmodule

module UniversalShiftRegister (
  input  CLK,
  input  LL,
  input  LH,
  input  SB,
  input  S1,
  input  S2,
  input  [9:0] I,
  output [9:0] O
);

  wire mux4to1_1_o, mux4to1_2_o, mux4to1_3_o, mux4to1_4_o, mux4to1_5_o, mux4to1_6_o, mux4to1_7_o,
       mux4to1_8_o, mux4to1_9_o, mux4to1_10_o, nand_1_out, nand_2_out, nand_3_out, nand_4_out;

  nand nand_1 (nand_1_out, CLK, LL);
  nand nand_2 (nand_2_out, nand_1_out, nand_1_out);
  nand nand_3 (nand_3_out, CLK, LH);
  nand nand_4 (nand_4_out, nand_3_out, nand_3_out);
  Mux4To1 mux4to1_1 (.A(O[1]), .B(1'b0), .C(I[0]), .D(1'b0), .S1(S1), .S2(S2), .O(mux4to1_1_o));
  DFlipFlop dflipflop_1 (.CLK(nand_2_out), .D(mux4to1_1_o), .SB(SB), .O(O[0]));  // open: OC
  Mux4To1 mux4to1_2 (.A(O[2]), .B(O[0]), .C(I[1]), .D(1'b0), .S1(S1), .S2(S2), .O(mux4to1_2_o));
  DFlipFlop dflipflop_2 (.CLK(nand_2_out), .D(mux4to1_2_o), .SB(SB), .O(O[1]));  // open: OC
  Mux4To1 mux4to1_3 (.A(O[3]), .B(O[1]), .C(I[2]), .D(1'b0), .S1(S1), .S2(S2), .O(mux4to1_3_o));
  DFlipFlop dflipflop_3 (.CLK(nand_2_out), .D(mux4to1_3_o), .SB(SB), .O(O[2]));  // open: OC
  Mux4To1 mux4to1_4 (.A(O[4]), .B(O[2]), .C(I[3]), .D(1'b0), .S1(S1), .S2(S2), .O(mux4to1_4_o));
  DFlipFlop dflipflop_4 (.CLK(nand_2_out), .D(mux4to1_4_o), .SB(SB), .O(O[3]));  // open: OC
  Mux4To1 mux4to1_5 (.A(O[5]), .B(O[3]), .C(I[4]), .D(1'b0), .S1(S1), .S2(S2), .O(mux4to1_5_o));
  DFlipFlop dflipflop_5 (.CLK(nand_2_out), .D(mux4to1_5_o), .SB(SB), .O(O[4]));  // open: OC
  Mux4To1 mux4to1_6 (.A(O[6]), .B(O[4]), .C(I[5]), .D(1'b0), .S1(S1), .S2(S2), .O(mux4to1_6_o));
  DFlipFlop dflipflop_6 (.CLK(nand_4_out), .D(mux4to1_6_o), .SB(SB), .O(O[5]));  // open: OC
  Mux4To1 mux4to1_7 (.A(O[7]), .B(O[5]), .C(I[6]), .D(1'b0), .S1(S1), .S2(S2), .O(mux4to1_7_o));
  DFlipFlop dflipflop_7 (.CLK(nand_4_out), .D(mux4to1_7_o), .SB(SB), .O(O[6]));  // open: OC
  Mux4To1 mux4to1_8 (.A(O[8]), .B(O[6]), .C(I[7]), .D(1'b0), .S1(S1), .S2(S2), .O(mux4to1_8_o));
  DFlipFlop dflipflop_8 (.CLK(nand_4_out), .D(mux4to1_8_o), .SB(SB), .O(O[7]));  // open: OC
  Mux4To1 mux4to1_9 (.A(O[9]), .B(O[7]), .C(I[8]), .D(1'b0), .S1(S1), .S2(S2), .O(mux4to1_9_o));
  DFlipFlop dflipflop_9 (.CLK(nand_4_out), .D(mux4to1_9_o), .SB(SB), .O(O[8]));  // open: OC
  Mux4To1 mux4to1_10 (.A(1'b0), .B(O[8]), .C(I[9]), .D(1'b0), .S1(S1), .S2(S2), .O(mux4to1_10_o));
  DFlipFlop dflipflop_10 (.CLK(nand_4_out), .D(mux4to1_10_o), .SB(SB), .O(O[9]));  // open: OC
endmodule

module Mux2To1 (
  input  A,
  input  B,
  input  S,
  output O
);

  wire nand_1_out, nand_2_out, nand_3_out;

  nand nand_1 (nand_1_out, S, S);
  nand nand_2 (nand_2_out, A, nand_1_out);
  nand nand_3 (nand_3_out, B, S);
  nand nand_4 (O, nand_2_out, nand_3_out);
endmodule

module Mux4To1 (
  input  A,
  input  B,
  input  C,
  input  D,
  input  S1,
  input  S2,
  output O
);

  wire mux2to1_1_o, mux2to1_2_o;

  Mux2To1 mux2to1_1 (.A(A), .B(C), .S(S1), .O(mux2to1_1_o));
  Mux2To1 mux2to1_2 (.A(B), .B(D), .S(S1), .O(mux2to1_2_o));
  Mux2To1 mux2to1_3 (.A(mux2to1_1_o), .B(mux2to1_2_o), .S(S2), .O(O));
endmodule

module DFlipFlop (
  input  CLK,
  input  D,
  input  SB,
  output O,
  output OC
);

  wire dlatch_1_o, nand_1_out;

  DLatch dlatch_1 (.E(CLK), .D(D), .SB(SB), .O(dlatch_1_o));  // open: OC
  nand nand_1 (nand_1_out, CLK, CLK);
  DLatch dlatch_2 (.E(nand_1_out), .D(dlatch_1_o), .SB(SB), .O(O), .OC(OC));
endmodule

module NormalRegister (
  input  CLK,
  input  LL,
  input  LH,
  input  SB,
  input  [9:0] I,
  output [9:0] O
);

  wire nand_1_out, nand_2_out, nand_3_out, nand_4_out;

  nand nand_1 (nand_1_out, CLK, LL);
  nand nand_2 (nand_2_out, nand_1_out, nand_1_out);
  nand nand_3 (nand_3_out, CLK, LH);
  nand nand_4 (nand_4_out, nand_3_out, nand_3_out);
  DFlipFlop dflipflop_1 (.CLK(nand_2_out), .D(I[0]), .SB(SB), .O(O[0]));  // open: OC
  DFlipFlop dflipflop_2 (.CLK(nand_2_out), .D(I[1]), .SB(SB), .O(O[1]));  // open: OC
  DFlipFlop dflipflop_3 (.CLK(nand_2_out), .D(I[2]), .SB(SB), .O(O[2]));  // open: OC
  DFlipFlop dflipflop_4 (.CLK(nand_2_out), .D(I[3]), .SB(SB), .O(O[3]));  // open: OC
  DFlipFlop dflipflop_5 (.CLK(nand_2_out), .D(I[4]), .SB(SB), .O(O[4]));  // open: OC
  DFlipFlop dflipflop_6 (.CLK(nand_4_out), .D(I[5]), .SB(SB), .O(O[5]));  // open: OC
  DFlipFlop dflipflop_7 (.CLK(nand_4_out), .D(I[6]), .SB(SB), .O(O[6]));  // open: OC
  DFlipFlop dflipflop_8 (.CLK(nand_4_out), .D(I[7]), .SB(SB), .O(O[7]));  // open: OC
  DFlipFlop dflipflop_9 (.CLK(nand_4_out), .D(I[8]), .SB(SB), .O(O[8]));  // open: OC
  DFlipFlop dflipflop_10 (.CLK(nand_4_out), .D(I[9]), .SB(SB), .O(O[9]));  // open: OC
endmodule

module SyncCounter (
  input  SB,
  input  CLK,
  input  ENABLE,
  input  L,
  input  [19:0] I,
  output [19:0] O
);

  wire jkflipflop_12_o, mux2to1_1_o, mux2to1_2_o, mux2to1_3_o, mux2to1_4_o, mux2to1_5_o, mux2to1_6_o,
       mux2to1_7_o, mux2to1_8_o, mux2to1_9_o, mux2to1_10_o, mux2to1_11_o, mux2to1_12_o, mux2to1_13_o,
       mux2to1_14_o, mux2to1_15_o, mux2to1_16_o, mux2to1_17_o, mux2to1_18_o, mux2to1_19_o, mux2to1_20_o,
       mux2to1_21_o, mux2to1_22_o, mux2to1_23_o, mux2to1_24_o, mux2to1_25_o, mux2to1_26_o, mux2to1_27_o,
       mux2to1_28_o, mux2to1_29_o, mux2to1_30_o, mux2to1_31_o, mux2to1_32_o, mux2to1_33_o, mux2to1_34_o,
       mux2to1_35_o, mux2to1_36_o, mux2to1_37_o, mux2to1_38_o, mux2to1_39_o, mux2to1_40_o, nand_1_out,
       nand_2_out, nand_3_out, nand_4_out, nand_5_out, nand_6_out, nand_7_out, nand_8_out, nand_9_out,
       nand_10_out, nand_11_out, nand_12_out, nand_13_out, nand_14_out, nand_15_out, nand_16_out,
       nand_17_out, nand_18_out, nand_19_out, nand_20_out, nand_21_out, nand_22_out, nand_23_out,
       nand_24_out, nand_25_out, nand_26_out, nand_27_out, nand_28_out, nand_29_out, nand_30_out,
       nand_31_out, nand_32_out, nand_33_out, nand_34_out, nand_35_out, nand_36_out, nand_37_out,
       nand_38_out, nand_39_out, nand_40_out, nand_41_out, nand_42_out, nand_43_out, nand_44_out,
       nand_45_out, nand_46_out, nand_47_out, nand_48_out, nand_49_out, nand_50_out, nand_51_out,
       nand_52_out, nand_53_out, nand_54_out, nand_55_out, nand_56_out, nand_57_out, nand_58_out,
       nand_59_out, nand_60_out;

  nand nand_1 (nand_1_out, CLK, ENABLE);
  nand nand_2 (nand_2_out, nand_1_out, nand_1_out);
  JKFlipFlop jkflipflop_1 (.SB(SB), .J(1'b1), .CLK(nand_2_out), .K(1'b1), .O(O[0]));  // open: OC
  Mux2To1 mux2to1_1 (.A(O[0]), .B(I[0]), .S(L), .O(mux2to1_1_o));
  nand nand_3 (nand_3_out, mux2to1_1_o, mux2to1_1_o);
  Mux2To1 mux2to1_2 (.A(mux2to1_1_o), .B(nand_3_out), .S(L), .O(mux2to1_2_o));
  JKFlipFlop jkflipflop_2 (.SB(SB), .J(mux2to1_1_o), .CLK(nand_2_out), .K(mux2to1_2_o), .O(O[1]));  // open: OC
  nand nand_4 (nand_4_out, O[0], O[1]);
  nand nand_5 (nand_5_out, nand_4_out, nand_4_out);
  Mux2To1 mux2to1_3 (.A(nand_5_out), .B(I[1]), .S(L), .O(mux2to1_3_o));
  nand nand_6 (nand_6_out, mux2to1_3_o, mux2to1_3_o);
  Mux2To1 mux2to1_4 (.A(mux2to1_3_o), .B(nand_6_out), .S(L), .O(mux2to1_4_o));
  JKFlipFlop jkflipflop_3 (.SB(SB), .J(mux2to1_3_o), .CLK(nand_2_out), .K(mux2to1_4_o), .O(O[2]));  // open: OC
  nand nand_7 (nand_7_out, nand_5_out, O[2]);
  nand nand_8 (nand_8_out, nand_7_out, nand_7_out);
  Mux2To1 mux2to1_5 (.A(nand_8_out), .B(I[2]), .S(L), .O(mux2to1_5_o));
  nand nand_9 (nand_9_out, mux2to1_5_o, mux2to1_5_o);
  Mux2To1 mux2to1_6 (.A(mux2to1_5_o), .B(nand_9_out), .S(L), .O(mux2to1_6_o));
  JKFlipFlop jkflipflop_4 (.SB(SB), .J(mux2to1_5_o), .CLK(nand_2_out), .K(mux2to1_6_o), .O(O[3]));  // open: OC
  nand nand_10 (nand_10_out, nand_8_out, O[3]);
  nand nand_11 (nand_11_out, nand_10_out, nand_10_out);
  Mux2To1 mux2to1_7 (.A(nand_11_out), .B(I[3]), .S(L), .O(mux2to1_7_o));
  nand nand_12 (nand_12_out, mux2to1_7_o, mux2to1_7_o);
  Mux2To1 mux2to1_8 (.A(mux2to1_7_o), .B(nand_12_out), .S(L), .O(mux2to1_8_o));
  JKFlipFlop jkflipflop_5 (.SB(SB), .J(mux2to1_7_o), .CLK(nand_2_out), .K(mux2to1_8_o), .O(O[4]));  // open: OC
  nand nand_13 (nand_13_out, nand_11_out, O[4]);
  nand nand_14 (nand_14_out, nand_13_out, nand_13_out);
  Mux2To1 mux2to1_9 (.A(nand_14_out), .B(I[4]), .S(L), .O(mux2to1_9_o));
  nand nand_15 (nand_15_out, mux2to1_9_o, mux2to1_9_o);
  Mux2To1 mux2to1_10 (.A(mux2to1_9_o), .B(nand_15_out), .S(L), .O(mux2to1_10_o));
  JKFlipFlop jkflipflop_6 (.SB(SB), .J(mux2to1_9_o), .CLK(nand_2_out), .K(mux2to1_10_o), .O(O[5]));  // open: OC
  nand nand_16 (nand_16_out, nand_14_out, O[5]);
  nand nand_17 (nand_17_out, nand_16_out, nand_16_out);
  Mux2To1 mux2to1_11 (.A(nand_17_out), .B(I[5]), .S(L), .O(mux2to1_11_o));
  nand nand_18 (nand_18_out, mux2to1_11_o, mux2to1_11_o);
  Mux2To1 mux2to1_12 (.A(mux2to1_11_o), .B(nand_18_out), .S(L), .O(mux2to1_12_o));
  JKFlipFlop jkflipflop_7 (.SB(SB), .J(mux2to1_11_o), .CLK(nand_2_out), .K(mux2to1_12_o), .O(O[6]));  // open: OC
  nand nand_19 (nand_19_out, nand_17_out, O[6]);
  nand nand_20 (nand_20_out, nand_19_out, nand_19_out);
  Mux2To1 mux2to1_13 (.A(nand_20_out), .B(I[6]), .S(L), .O(mux2to1_13_o));
  nand nand_21 (nand_21_out, mux2to1_13_o, mux2to1_13_o);
  Mux2To1 mux2to1_14 (.A(mux2to1_13_o), .B(nand_21_out), .S(L), .O(mux2to1_14_o));
  JKFlipFlop jkflipflop_8 (.SB(SB), .J(mux2to1_13_o), .CLK(nand_2_out), .K(mux2to1_14_o), .O(O[7]));  // open: OC
  nand nand_22 (nand_22_out, nand_20_out, O[7]);
  nand nand_23 (nand_23_out, nand_22_out, nand_22_out);
  Mux2To1 mux2to1_15 (.A(nand_23_out), .B(I[7]), .S(L), .O(mux2to1_15_o));
  nand nand_24 (nand_24_out, mux2to1_15_o, mux2to1_15_o);
  Mux2To1 mux2to1_16 (.A(mux2to1_15_o), .B(nand_24_out), .S(L), .O(mux2to1_16_o));
  JKFlipFlop jkflipflop_9 (.SB(SB), .J(mux2to1_15_o), .CLK(nand_2_out), .K(mux2to1_16_o), .O(O[8]));  // open: OC
  nand nand_25 (nand_25_out, nand_23_out, O[8]);
  nand nand_26 (nand_26_out, nand_25_out, nand_25_out);
  Mux2To1 mux2to1_17 (.A(nand_26_out), .B(I[8]), .S(L), .O(mux2to1_17_o));
  nand nand_27 (nand_27_out, mux2to1_17_o, mux2to1_17_o);
  Mux2To1 mux2to1_18 (.A(mux2to1_17_o), .B(nand_27_out), .S(L), .O(mux2to1_18_o));
  JKFlipFlop jkflipflop_10 (.SB(SB), .J(mux2to1_17_o), .CLK(nand_2_out), .K(mux2to1_18_o), .O(O[9]));  // open: OC
  nand nand_28 (nand_28_out, nand_26_out, O[9]);
  nand nand_29 (nand_29_out, nand_28_out, nand_28_out);
  Mux2To1 mux2to1_19 (.A(nand_29_out), .B(I[9]), .S(L), .O(mux2to1_19_o));
  nand nand_30 (nand_30_out, mux2to1_19_o, mux2to1_19_o);
  Mux2To1 mux2to1_20 (.A(mux2to1_19_o), .B(nand_30_out), .S(L), .O(mux2to1_20_o));
  JKFlipFlop jkflipflop_11 (.SB(SB), .J(mux2to1_19_o), .CLK(nand_2_out), .K(mux2to1_20_o), .O(O[10]));  // open: OC
  nand nand_31 (nand_31_out, nand_29_out, O[10]);
  nand nand_32 (nand_32_out, nand_31_out, nand_31_out);
  Mux2To1 mux2to1_21 (.A(nand_32_out), .B(I[10]), .S(L), .O(mux2to1_21_o));
  nand nand_33 (nand_33_out, mux2to1_21_o, mux2to1_21_o);
  Mux2To1 mux2to1_22 (.A(mux2to1_21_o), .B(nand_33_out), .S(L), .O(mux2to1_22_o));
  JKFlipFlop jkflipflop_12 (
    .SB(SB), .J(mux2to1_21_o), .CLK(nand_2_out), .K(mux2to1_22_o), .O(jkflipflop_12_o));  // open: OC
  nand nand_34 (nand_34_out, nand_32_out, jkflipflop_12_o);
  nand nand_35 (nand_35_out, nand_34_out, nand_34_out);
  Mux2To1 mux2to1_23 (.A(nand_35_out), .B(I[11]), .S(L), .O(mux2to1_23_o));
  nand nand_36 (nand_36_out, mux2to1_23_o, mux2to1_23_o);
  Mux2To1 mux2to1_24 (.A(mux2to1_23_o), .B(nand_36_out), .S(L), .O(mux2to1_24_o));
  JKFlipFlop jkflipflop_13 (.SB(SB), .J(mux2to1_23_o), .CLK(nand_2_out), .K(mux2to1_24_o), .O(O[11]));  // open: OC
  nand nand_37 (nand_37_out, nand_35_out, O[11]);
  nand nand_38 (nand_38_out, nand_37_out, nand_37_out);
  Mux2To1 mux2to1_25 (.A(nand_38_out), .B(I[12]), .S(L), .O(mux2to1_25_o));
  nand nand_39 (nand_39_out, mux2to1_25_o, mux2to1_25_o);
  Mux2To1 mux2to1_26 (.A(mux2to1_25_o), .B(nand_39_out), .S(L), .O(mux2to1_26_o));
  JKFlipFlop jkflipflop_14 (.SB(SB), .J(mux2to1_25_o), .CLK(nand_2_out), .K(mux2to1_26_o), .O(O[12]));  // open: OC
  nand nand_40 (nand_40_out, nand_38_out, O[12]);
  nand nand_41 (nand_41_out, nand_40_out, nand_40_out);
  Mux2To1 mux2to1_27 (.A(nand_41_out), .B(I[13]), .S(L), .O(mux2to1_27_o));
  nand nand_42 (nand_42_out, mux2to1_27_o, mux2to1_27_o);
  Mux2To1 mux2to1_28 (.A(mux2to1_27_o), .B(nand_42_out), .S(L), .O(mux2to1_28_o));
  JKFlipFlop jkflipflop_15 (.SB(SB), .J(mux2to1_27_o), .CLK(nand_2_out), .K(mux2to1_28_o), .O(O[13]));  // open: OC
  nand nand_43 (nand_43_out, nand_41_out, O[13]);
  nand nand_44 (nand_44_out, nand_43_out, nand_43_out);
  Mux2To1 mux2to1_29 (.A(nand_44_out), .B(I[14]), .S(L), .O(mux2to1_29_o));
  nand nand_45 (nand_45_out, mux2to1_29_o, mux2to1_29_o);
  Mux2To1 mux2to1_30 (.A(mux2to1_29_o), .B(nand_45_out), .S(L), .O(mux2to1_30_o));
  JKFlipFlop jkflipflop_16 (.SB(SB), .J(mux2to1_29_o), .CLK(nand_2_out), .K(mux2to1_30_o), .O(O[14]));  // open: OC
  nand nand_46 (nand_46_out, nand_44_out, O[14]);
  nand nand_47 (nand_47_out, nand_46_out, nand_46_out);
  Mux2To1 mux2to1_31 (.A(nand_47_out), .B(I[15]), .S(L), .O(mux2to1_31_o));
  nand nand_48 (nand_48_out, mux2to1_31_o, mux2to1_31_o);
  Mux2To1 mux2to1_32 (.A(mux2to1_31_o), .B(nand_48_out), .S(L), .O(mux2to1_32_o));
  JKFlipFlop jkflipflop_17 (.SB(SB), .J(mux2to1_31_o), .CLK(nand_2_out), .K(mux2to1_32_o), .O(O[15]));  // open: OC
  nand nand_49 (nand_49_out, nand_47_out, O[15]);
  nand nand_50 (nand_50_out, nand_49_out, nand_49_out);
  Mux2To1 mux2to1_33 (.A(nand_50_out), .B(I[16]), .S(L), .O(mux2to1_33_o));
  nand nand_51 (nand_51_out, mux2to1_33_o, mux2to1_33_o);
  Mux2To1 mux2to1_34 (.A(mux2to1_33_o), .B(nand_51_out), .S(L), .O(mux2to1_34_o));
  JKFlipFlop jkflipflop_18 (.SB(SB), .J(mux2to1_33_o), .CLK(nand_2_out), .K(mux2to1_34_o), .O(O[16]));  // open: OC
  nand nand_52 (nand_52_out, nand_50_out, O[16]);
  nand nand_53 (nand_53_out, nand_52_out, nand_52_out);
  Mux2To1 mux2to1_35 (.A(nand_53_out), .B(I[17]), .S(L), .O(mux2to1_35_o));
  nand nand_54 (nand_54_out, mux2to1_35_o, mux2to1_35_o);
  Mux2To1 mux2to1_36 (.A(mux2to1_35_o), .B(nand_54_out), .S(L), .O(mux2to1_36_o));
  JKFlipFlop jkflipflop_19 (.SB(SB), .J(mux2to1_35_o), .CLK(nand_2_out), .K(mux2to1_36_o), .O(O[17]));  // open: OC
  nand nand_55 (nand_55_out, nand_53_out, O[17]);
  nand nand_56 (nand_56_out, nand_55_out, nand_55_out);
  Mux2To1 mux2to1_37 (.A(nand_56_out), .B(I[18]), .S(L), .O(mux2to1_37_o));
  nand nand_57 (nand_57_out, mux2to1_37_o, mux2to1_37_o);
  Mux2To1 mux2to1_38 (.A(mux2to1_37_o), .B(nand_57_out), .S(L), .O(mux2to1_38_o));
  JKFlipFlop jkflipflop_20 (.SB(SB), .J(mux2to1_37_o), .CLK(nand_2_out), .K(mux2to1_38_o), .O(O[18]));  // open: OC
  nand nand_58 (nand_58_out, nand_56_out, O[18]);
  nand nand_59 (nand_59_out, nand_58_out, nand_58_out);
  Mux2To1 mux2to1_39 (.A(nand_59_out), .B(I[19]), .S(L), .O(mux2to1_39_o));
  nand nand_60 (nand_60_out, mux2to1_39_o, mux2to1_39_o);
  Mux2To1 mux2to1_40 (.A(mux2to1_39_o), .B(nand_60_out), .S(L), .O(mux2to1_40_o));
  JKFlipFlop jkflipflop_21 (.SB(SB), .J(mux2to1_39_o), .CLK(nand_2_out), .K(mux2to1_40_o), .O(O[19]));  // open: OC
endmodule

module JKFlipFlop (
  input  SB,
  input  J,
  input  CLK,
  input  K,
  output O,
  output OC
);

  wire nand_1_out, nand_2_out, nand_3_out, nand_4_out, nand_5_out, nand_6_out, nand_7_out, nand_8_out,
       nand_9_out, nand_10_out, nand_11_out;

  nand nand_1 (nand_1_out, OC, J);
  nand nand_2 (nand_2_out, K, O);
  nand nand_3 (nand_3_out, nand_1_out, nand_1_out);
  nand nand_4 (nand_4_out, nand_2_out, nand_2_out);
  nand nand_5 (nand_5_out, nand_3_out, CLK);
  nand nand_6 (nand_6_out, CLK, nand_4_out);
  nand nand_7 (nand_7_out, nand_5_out, nand_8_out);
  nand nand_8 (nand_8_out, nand_7_out, SB, nand_6_out);
  nand nand_9 (nand_9_out, CLK, CLK);
  nand nand_10 (nand_10_out, nand_7_out, nand_9_out);
  nand nand_11 (nand_11_out, nand_9_out, nand_8_out);
  nand nand_12 (O, nand_10_out, OC);
  nand nand_13 (OC, O, SB, nand_11_out);
endmodule

module ALU (
  input  [9:0] A,
  input  [9:0] B,
  input  AZ,
  input  AC,
  input  BZ,
  input  BC,
  input  Cin,
  input  N,
  input  OC,
  output Cout,
  output [9:0] O
);

  wire [9:0] fulladder10_1_o, inverter10_1_o, inverter10_2_o, inverter10_3_o, mux2to1_10_1_o, mux2to1_10_2_o,
       mux2to1_10_3_o, mux2to1_10_4_o, mux2to1_10_5_o, nand10_1_o;

  Mux2To1_10 mux2to1_10_1 (.A(A), .B({10{1'b0}}), .S(AZ), .O(mux2to1_10_1_o));
  Mux2To1_10 mux2to1_10_2 (.A(B), .B({10{1'b0}}), .S(BZ), .O(mux2to1_10_2_o));
  Inverter10 inverter10_1 (.I(mux2to1_10_1_o), .O(inverter10_1_o));
  Inverter10 inverter10_2 (.I(mux2to1_10_2_o), .O(inverter10_2_o));
  Mux2To1_10 mux2to1_10_3 (.A(mux2to1_10_1_o), .B(inverter10_1_o), .S(AC), .O(mux2to1_10_3_o));
  Mux2To1_10 mux2to1_10_4 (.A(mux2to1_10_2_o), .B(inverter10_2_o), .S(BC), .O(mux2to1_10_4_o));
  FullAdder10 fulladder10_1 (.Cin(Cin), .A(mux2to1_10_3_o), .B(mux2to1_10_4_o), .O(fulladder10_1_o), .Cout(Cout));
  Nand10 nand10_1 (.A(mux2to1_10_3_o), .B(mux2to1_10_4_o), .O(nand10_1_o));
  Mux2To1_10 mux2to1_10_5 (.A(fulladder10_1_o), .B(nand10_1_o), .S(N), .O(mux2to1_10_5_o));
  Inverter10 inverter10_3 (.I(mux2to1_10_5_o), .O(inverter10_3_o));
  Mux2To1_10 mux2to1_10_6 (.A(mux2to1_10_5_o), .B(inverter10_3_o), .S(OC), .O(O));
endmodule

module Mux2To1_10 (
  input  [9:0] A,
  input  [9:0] B,
  input  S,
  output [9:0] O
);

  Mux2To1 mux2to1_1 (.A(A[0]), .B(B[0]), .S(S), .O(O[0]));
  Mux2To1 mux2to1_2 (.A(A[1]), .B(B[1]), .S(S), .O(O[1]));
  Mux2To1 mux2to1_3 (.A(A[2]), .B(B[2]), .S(S), .O(O[2]));
  Mux2To1 mux2to1_4 (.A(A[3]), .B(B[3]), .S(S), .O(O[3]));
  Mux2To1 mux2to1_5 (.A(A[4]), .B(B[4]), .S(S), .O(O[4]));
  Mux2To1 mux2to1_6 (.A(A[5]), .B(B[5]), .S(S), .O(O[5]));
  Mux2To1 mux2to1_7 (.A(A[6]), .B(B[6]), .S(S), .O(O[6]));
  Mux2To1 mux2to1_8 (.A(A[7]), .B(B[7]), .S(S), .O(O[7]));
  Mux2To1 mux2to1_9 (.A(A[8]), .B(B[8]), .S(S), .O(O[8]));
  Mux2To1 mux2to1_10 (.A(A[9]), .B(B[9]), .S(S), .O(O[9]));
endmodule

module Inverter10 (
  input  [9:0] I,
  output [9:0] O
);

  Nand10 nand10_1 (.A(I), .B(I), .O(O));
endmodule

module FullAdder (
  input  A,
  input  B,
  input  Cin,
  output O,
  output Cout
);

  wire nand_1_out, nand_2_out, nand_3_out, nand_4_out, nand_5_out, nand_6_out, nand_7_out, nand_8_out,
       nand_9_out, nand_10_out, nand_11_out;

  nand nand_1 (nand_1_out, A, A);
  nand nand_2 (nand_2_out, B, B);
  nand nand_3 (nand_3_out, B, A);
  nand nand_4 (nand_4_out, A, nand_2_out);
  nand nand_5 (nand_5_out, nand_1_out, B);
  nand nand_6 (nand_6_out, nand_4_out, nand_5_out);
  nand nand_7 (nand_7_out, nand_6_out, nand_6_out);
  nand nand_8 (nand_8_out, Cin, Cin);
  nand nand_9 (nand_9_out, Cin, nand_6_out);
  nand nand_10 (nand_10_out, nand_6_out, nand_8_out);
  nand nand_11 (nand_11_out, nand_7_out, Cin);
  nand nand_12 (O, nand_10_out, nand_11_out);
  nand nand_13 (Cout, nand_9_out, nand_3_out);
endmodule

module HalfAdder (
  input  A,
  input  B,
  output S,
  output C
);

  wire nand_1_out, nand_2_out, nand_3_out, nand_5_out, nand_6_out;

  nand nand_1 (nand_1_out, A, A);
  nand nand_2 (nand_2_out, B, B);
  nand nand_3 (nand_3_out, B, A);
  nand nand_4 (C, nand_3_out, nand_3_out);
  nand nand_5 (nand_5_out, A, nand_2_out);
  nand nand_6 (nand_6_out, nand_1_out, B);
  nand nand_7 (S, nand_5_out, nand_6_out);
endmodule

module FullAdder10 (
  input  Cin,
  input  [9:0] A,
  input  [9:0] B,
  output [9:0] O,
  output Cout
);

  wire fulladder_1_cout, fulladder_2_cout, fulladder_3_cout, fulladder_4_cout, fulladder_5_cout,
       fulladder_6_cout, fulladder_7_cout, fulladder_8_cout, fulladder_9_cout;

  FullAdder fulladder_1 (.A(A[0]), .B(B[0]), .Cin(Cin), .O(O[0]), .Cout(fulladder_1_cout));
  FullAdder fulladder_2 (.A(A[1]), .B(B[1]), .Cin(fulladder_1_cout), .O(O[1]), .Cout(fulladder_2_cout));
  FullAdder fulladder_3 (.A(A[2]), .B(B[2]), .Cin(fulladder_2_cout), .O(O[2]), .Cout(fulladder_3_cout));
  FullAdder fulladder_4 (.A(A[3]), .B(B[3]), .Cin(fulladder_3_cout), .O(O[3]), .Cout(fulladder_4_cout));
  FullAdder fulladder_5 (.A(A[4]), .B(B[4]), .Cin(fulladder_4_cout), .O(O[4]), .Cout(fulladder_5_cout));
  FullAdder fulladder_6 (.A(A[5]), .B(B[5]), .Cin(fulladder_5_cout), .O(O[5]), .Cout(fulladder_6_cout));
  FullAdder fulladder_7 (.A(A[6]), .B(B[6]), .Cin(fulladder_6_cout), .O(O[6]), .Cout(fulladder_7_cout));
  FullAdder fulladder_8 (.A(A[7]), .B(B[7]), .Cin(fulladder_7_cout), .O(O[7]), .Cout(fulladder_8_cout));
  FullAdder fulladder_9 (.A(A[8]), .B(B[8]), .Cin(fulladder_8_cout), .O(O[8]), .Cout(fulladder_9_cout));
  FullAdder fulladder_10 (.A(A[9]), .B(B[9]), .Cin(fulladder_9_cout), .O(O[9]), .Cout(Cout));
endmodule

module Nand10 (
  input  [9:0] A,
  input  [9:0] B,
  output [9:0] O
);

  nand nand_1 (O[0], A[0], B[0]);
  nand nand_2 (O[1], A[1], B[1]);
  nand nand_3 (O[2], A[2], B[2]);
  nand nand_4 (O[3], A[3], B[3]);
  nand nand_5 (O[4], A[4], B[4]);
  nand nand_6 (O[5], A[5], B[5]);
  nand nand_7 (O[6], A[6], B[6]);
  nand nand_8 (O[7], A[7], B[7]);
  nand nand_9 (O[8], A[8], B[8]);
  nand nand_10 (O[9], A[9], B[9]);
endmodule

module Buffer10 (
  input  [9:0] I,
  input  E,
  output [9:0] O
);

  assign O[0] = E ? I[0] : 1'bz;  // Controlled_Buffer controlled_buffer_1
  assign O[1] = E ? I[1] : 1'bz;  // Controlled_Buffer controlled_buffer_2
  assign O[2] = E ? I[2] : 1'bz;  // Controlled_Buffer controlled_buffer_3
  assign O[3] = E ? I[3] : 1'bz;  // Controlled_Buffer controlled_buffer_4
  assign O[4] = E ? I[4] : 1'bz;  // Controlled_Buffer controlled_buffer_5
  assign O[5] = E ? I[5] : 1'bz;  // Controlled_Buffer controlled_buffer_6
  assign O[6] = E ? I[6] : 1'bz;  // Controlled_Buffer controlled_buffer_7
  assign O[7] = E ? I[7] : 1'bz;  // Controlled_Buffer controlled_buffer_8
  assign O[8] = E ? I[8] : 1'bz;  // Controlled_Buffer controlled_buffer_9
  assign O[9] = E ? I[9] : 1'bz;  // Controlled_Buffer controlled_buffer_10
endmodule

module ALUFlagsRegister (
  input  CLK,
  input  LL,
  input  LH,
  input  SB,
  input  [6:0] I,
  output [6:0] O
);

  wire nand_1_out, nand_2_out, nand_3_out, nand_4_out;

  nand nand_1 (nand_1_out, CLK, LL);
  nand nand_2 (nand_2_out, nand_1_out, nand_1_out);
  nand nand_3 (nand_3_out, CLK, LH);
  nand nand_4 (nand_4_out, nand_3_out, nand_3_out);
  DLatch dlatch_1 (.E(nand_2_out), .D(I[0]), .SB(SB), .O(O[0]));  // open: OC
  DLatch dlatch_2 (.E(nand_2_out), .D(I[1]), .SB(SB), .O(O[1]));  // open: OC
  DLatch dlatch_3 (.E(nand_2_out), .D(I[2]), .SB(SB), .O(O[2]));  // open: OC
  DLatch dlatch_4 (.E(nand_2_out), .D(I[3]), .SB(SB), .O(O[3]));  // open: OC
  DLatch dlatch_5 (.E(nand_2_out), .D(I[4]), .SB(SB), .O(O[4]));  // open: OC
  DLatch dlatch_6 (.E(nand_4_out), .D(I[5]), .SB(SB), .O(O[5]));  // open: OC
  DLatch dlatch_7 (.E(nand_4_out), .D(I[6]), .SB(SB), .O(O[6]));  // open: OC
endmodule

module Mux2To1_20 (
  input  [19:0] A,
  input  [19:0] B,
  input  S,
  output [19:0] O
);

  Mux2To1_10 mux2to1_10_1 (.A(A[9:0]), .B(B[9:0]), .S(S), .O(O[9:0]));
  Mux2To1_10 mux2to1_10_2 (.A(A[19:10]), .B(B[19:10]), .S(S), .O(O[19:10]));
endmodule

module Buffer20 (
  input  [19:0] I,
  input  E,
  output [19:0] O
);

  Buffer10 buffer10_1 (.I(I[9:0]), .E(E), .O(O[9:0]));
  Buffer10 buffer10_2 (.I(I[19:10]), .E(E), .O(O[19:10]));
endmodule

module NormalRegister20 (
  input  CLK,
  input  LLL,
  input  LLH,
  input  LHL,
  input  LHH,
  input  SB,
  input  [9:0] IL,
  input  [9:0] IH,
  output [19:0] O
);

  NormalRegister normalregister_1 (.CLK(CLK), .LL(LLL), .LH(LLH), .SB(SB), .I(IL), .O(O[9:0]));
  NormalRegister normalregister_2 (.CLK(CLK), .LL(LHL), .LH(LHH), .SB(SB), .I(IH), .O(O[19:10]));
endmodule

module NormalRegister4 (
  input  CLK,
  input  LOAD,
  input  SB,
  input  [3:0] I,
  output [3:0] O
);

  wire nand_1_out, nand_2_out;

  nand nand_1 (nand_1_out, CLK, LOAD);
  nand nand_2 (nand_2_out, nand_1_out, nand_1_out);
  DLatch dlatch_1 (.E(nand_2_out), .D(I[0]), .SB(SB), .O(O[0]));  // open: OC
  DLatch dlatch_2 (.E(nand_2_out), .D(I[1]), .SB(SB), .O(O[1]));  // open: OC
  DLatch dlatch_3 (.E(nand_2_out), .D(I[2]), .SB(SB), .O(O[2]));  // open: OC
  DLatch dlatch_4 (.E(nand_2_out), .D(I[3]), .O(O[3]));  // open: SB, OC
endmodule

module Buffer4 (
  input  [3:0] I,
  input  E,
  output [3:0] O
);

  assign O[0] = E ? I[0] : 1'bz;  // Controlled_Buffer controlled_buffer_1
  assign O[1] = E ? I[1] : 1'bz;  // Controlled_Buffer controlled_buffer_2
  assign O[2] = E ? I[2] : 1'bz;  // Controlled_Buffer controlled_buffer_3
  assign O[3] = E ? I[3] : 1'bz;  // Controlled_Buffer controlled_buffer_4
endmodule

module NormalRegister3 (
  input  CLK,
  input  LOAD,
  input  SB,
  input  [2:0] I,
  output [2:0] O
);

  wire nand_1_out, nand_2_out;

  nand nand_1 (nand_1_out, CLK, LOAD);
  nand nand_2 (nand_2_out, nand_1_out, nand_1_out);
  DLatch dlatch_1 (.E(nand_2_out), .D(I[0]), .SB(SB), .O(O[0]));  // open: OC
  DLatch dlatch_2 (.E(nand_2_out), .D(I[1]), .SB(SB), .O(O[1]));  // open: OC
  DLatch dlatch_3 (.E(nand_2_out), .D(I[2]), .SB(SB), .O(O[2]));  // open: OC
endmodule

module Or10 (
  input  [9:0] I,
  output O
);

  wire nand_1_out, nand_2_out, nand_3_out, nand_4_out, nand_5_out, nand_6_out, nand_7_out, nand_8_out,
       nand_9_out, nand_10_out, nand_11_out, nand_12_out, nand_13_out, nand_14_out, nand_15_out, nand_16_out,
       nand_17_out, nand_18_out, nand_19_out, nand_20_out, nand_21_out, nand_22_out, nand_23_out,
       nand_24_out, nand_25_out, nand_26_out;

  nand nand_1 (nand_1_out, I[0], I[0]);
  nand nand_2 (nand_2_out, I[1], I[1]);
  nand nand_3 (nand_3_out, nand_1_out, nand_2_out);
  nand nand_4 (nand_4_out, nand_3_out, nand_3_out);
  nand nand_5 (nand_5_out, I[2], I[2]);
  nand nand_6 (nand_6_out, nand_4_out, nand_5_out);
  nand nand_7 (nand_7_out, nand_6_out, nand_6_out);
  nand nand_8 (nand_8_out, I[3], I[3]);
  nand nand_9 (nand_9_out, nand_7_out, nand_8_out);
  nand nand_10 (nand_10_out, nand_9_out, nand_9_out);
  nand nand_11 (nand_11_out, I[4], I[4]);
  nand nand_12 (nand_12_out, nand_10_out, nand_11_out);
  nand nand_13 (nand_13_out, nand_12_out, nand_12_out);
  nand nand_14 (nand_14_out, I[5], I[5]);
  nand nand_15 (nand_15_out, nand_13_out, nand_14_out);
  nand nand_16 (nand_16_out, nand_15_out, nand_15_out);
  nand nand_17 (nand_17_out, I[6], I[6]);
  nand nand_18 (nand_18_out, nand_16_out, nand_17_out);
  nand nand_19 (nand_19_out, nand_18_out, nand_18_out);
  nand nand_20 (nand_20_out, I[7], I[7]);
  nand nand_21 (nand_21_out, nand_19_out, nand_20_out);
  nand nand_22 (nand_22_out, nand_21_out, nand_21_out);
  nand nand_23 (nand_23_out, I[8], I[8]);
  nand nand_24 (nand_24_out, nand_22_out, nand_23_out);
  nand nand_25 (nand_25_out, nand_24_out, nand_24_out);
  nand nand_26 (nand_26_out, I[9], I[9]);
  nand nand_27 (O, nand_25_out, nand_26_out);
endmodule

module Buffer37 (
  input  [36:0] I,
  input  E,
  output [36:0] O
);

  assign O[30] = E ? I[30] : 1'bz;  // Controlled_Buffer controlled_buffer_1
  assign O[31] = E ? I[31] : 1'bz;  // Controlled_Buffer controlled_buffer_2
  assign O[32] = E ? I[32] : 1'bz;  // Controlled_Buffer controlled_buffer_3
  assign O[33] = E ? I[33] : 1'bz;  // Controlled_Buffer controlled_buffer_4
  assign O[34] = E ? I[34] : 1'bz;  // Controlled_Buffer controlled_buffer_5
  assign O[35] = E ? I[35] : 1'bz;  // Controlled_Buffer controlled_buffer_6
  assign O[36] = E ? I[36] : 1'bz;  // Controlled_Buffer controlled_buffer_7
  Buffer10 buffer10_1 (.I(I[9:0]), .E(E), .O(O[9:0]));
  Buffer10 buffer10_2 (.I(I[19:10]), .E(E), .O(O[19:10]));
  Buffer10 buffer10_3 (.I(I[29:20]), .E(E), .O(O[29:20]));
endmodule

module And10 (
  input  [9:0] I,
  output O
);

  wire nand_1_out, nand_2_out, nand_3_out, nand_4_out, nand_5_out, nand_6_out, nand_7_out, nand_8_out,
       nand_9_out, nand_10_out, nand_11_out, nand_12_out, nand_13_out, nand_14_out, nand_15_out, nand_16_out,
       nand_17_out;

  nand nand_1 (nand_1_out, I[0], I[1]);
  nand nand_2 (nand_2_out, nand_1_out, nand_1_out);
  nand nand_3 (nand_3_out, nand_2_out, I[2]);
  nand nand_4 (nand_4_out, nand_3_out, nand_3_out);
  nand nand_5 (nand_5_out, nand_4_out, I[3]);
  nand nand_6 (nand_6_out, nand_5_out, nand_5_out);
  nand nand_7 (nand_7_out, nand_6_out, I[4]);
  nand nand_8 (nand_8_out, nand_7_out, nand_7_out);
  nand nand_9 (nand_9_out, nand_8_out, I[5]);
  nand nand_10 (nand_10_out, nand_9_out, nand_9_out);
  nand nand_11 (nand_11_out, nand_10_out, I[6]);
  nand nand_12 (nand_12_out, nand_11_out, nand_11_out);
  nand nand_13 (nand_13_out, nand_12_out, I[7]);
  nand nand_14 (nand_14_out, nand_13_out, nand_13_out);
  nand nand_15 (nand_15_out, nand_14_out, I[8]);
  nand nand_16 (nand_16_out, nand_15_out, nand_15_out);
  nand nand_17 (nand_17_out, nand_16_out, I[9]);
  nand nand_18 (O, nand_17_out, nand_17_out);
endmodule

module Demux1To2 (
  input  I,
  input  S,
  output A,
  output B
);

  wire nand_1_out, nand_2_out, nand_4_out;

  nand nand_1 (nand_1_out, S, S);
  nand nand_2 (nand_2_out, I, nand_1_out);
  nand nand_3 (A, nand_2_out, nand_2_out);
  nand nand_4 (nand_4_out, I, S);
  nand nand_5 (B, nand_4_out, nand_4_out);
endmodule

module Demux1To8S3 (
  input  I,
  input  [2:0] S,
  output [7:0] O
);

  wire and3_1_o, and3_2_o, and3_3_o, and3_4_o, and3_5_o, and3_6_o, and3_7_o, and3_8_o, nand_4_out,
       nand_5_out, nand_6_out, nand_7_out, nand_8_out, nand_9_out, nand_10_out, nand_11_out;
  wire [2:0] nand_3_out;

  nand nand_1 (nand_3_out[0], S[0], S[0]);
  nand nand_2 (nand_3_out[1], S[1], S[1]);
  nand nand_3 (nand_3_out[2], S[2], S[2]);
  And3 and3_1 (.I(nand_3_out), .O(and3_1_o));
  And3 and3_2 (.I({nand_3_out[2:1], S[0]}), .O(and3_2_o));
  And3 and3_3 (.I({nand_3_out[2], S[1], nand_3_out[0]}), .O(and3_3_o));
  And3 and3_4 (.I({nand_3_out[2], S[1:0]}), .O(and3_4_o));
  And3 and3_5 (.I({S[2], nand_3_out[1:0]}), .O(and3_5_o));
  And3 and3_6 (.I({S[2], nand_3_out[1], S[0]}), .O(and3_6_o));
  And3 and3_7 (.I({S[2:1], nand_3_out[0]}), .O(and3_7_o));
  And3 and3_8 (.I(S), .O(and3_8_o));
  nand nand_4 (nand_4_out, I, and3_1_o);
  nand nand_5 (nand_5_out, I, and3_2_o);
  nand nand_6 (nand_6_out, I, and3_3_o);
  nand nand_7 (nand_7_out, I, and3_4_o);
  nand nand_8 (nand_8_out, I, and3_5_o);
  nand nand_9 (nand_9_out, I, and3_6_o);
  nand nand_10 (nand_10_out, I, and3_7_o);
  nand nand_11 (nand_11_out, I, and3_8_o);
  nand nand_12 (O[0], nand_4_out, nand_4_out);
  nand nand_13 (O[1], nand_5_out, nand_5_out);
  nand nand_14 (O[2], nand_6_out, nand_6_out);
  nand nand_15 (O[3], nand_7_out, nand_7_out);
  nand nand_16 (O[4], nand_8_out, nand_8_out);
  nand nand_17 (O[5], nand_9_out, nand_9_out);
  nand nand_18 (O[6], nand_10_out, nand_10_out);
  nand nand_19 (O[7], nand_11_out, nand_11_out);
endmodule

module And3 (
  input  [2:0] I,
  output O
);

  wire nand_1_out, nand_2_out, nand_3_out;

  nand nand_1 (nand_1_out, I[0], I[1]);
  nand nand_2 (nand_2_out, nand_1_out, nand_1_out);
  nand nand_3 (nand_3_out, nand_2_out, I[2]);
  nand nand_4 (O, nand_3_out, nand_3_out);
endmodule

module Demux1To9S4 (
  input  I,
  input  [3:0] S,
  output [8:0] O
);

  wire and4_1_o, and4_2_o, and4_3_o, and4_4_o, and4_5_o, and4_6_o, and4_7_o, and4_8_o, and4_9_o, nand_5_out,
       nand_6_out, nand_7_out, nand_8_out, nand_9_out, nand_10_out, nand_11_out, nand_12_out, nand_13_out;
  wire [2:0] nand_1_out;
  wire [3:3] nand_4_out;

  nand nand_1 (nand_1_out[0], S[0], S[0]);
  nand nand_2 (nand_1_out[1], S[1], S[1]);
  nand nand_3 (nand_1_out[2], S[2], S[2]);
  nand nand_4 (nand_4_out[3], S[3], S[3]);
  And4 and4_1 (.I({nand_4_out[3], nand_1_out}), .O(and4_1_o));
  And4 and4_2 (.I({nand_4_out[3], nand_1_out[2:1], S[0]}), .O(and4_2_o));
  And4 and4_3 (.I({nand_4_out[3], nand_1_out[2], S[1], nand_1_out[0]}), .O(and4_3_o));
  And4 and4_4 (.I({nand_4_out[3], nand_1_out[2], S[1:0]}), .O(and4_4_o));
  And4 and4_5 (.I({nand_4_out[3], S[2], nand_1_out[1:0]}), .O(and4_5_o));
  And4 and4_6 (.I({nand_4_out[3], S[2], nand_1_out[1], S[0]}), .O(and4_6_o));
  And4 and4_7 (.I({nand_4_out[3], S[2:1], nand_1_out[0]}), .O(and4_7_o));
  And4 and4_8 (.I({nand_4_out[3], S[2:0]}), .O(and4_8_o));
  And4 and4_9 (.I({S[3], nand_1_out}), .O(and4_9_o));
  nand nand_5 (nand_5_out, I, and4_1_o);
  nand nand_6 (nand_6_out, I, and4_2_o);
  nand nand_7 (nand_7_out, I, and4_3_o);
  nand nand_8 (nand_8_out, I, and4_4_o);
  nand nand_9 (nand_9_out, I, and4_5_o);
  nand nand_10 (nand_10_out, I, and4_6_o);
  nand nand_11 (nand_11_out, I, and4_7_o);
  nand nand_12 (nand_12_out, I, and4_8_o);
  nand nand_13 (nand_13_out, I, and4_9_o);
  nand nand_14 (O[0], nand_5_out, nand_5_out);
  nand nand_15 (O[1], nand_6_out, nand_6_out);
  nand nand_16 (O[2], nand_7_out, nand_7_out);
  nand nand_17 (O[3], nand_8_out, nand_8_out);
  nand nand_18 (O[4], nand_9_out, nand_9_out);
  nand nand_19 (O[5], nand_10_out, nand_10_out);
  nand nand_20 (O[6], nand_11_out, nand_11_out);
  nand nand_21 (O[7], nand_12_out, nand_12_out);
  nand nand_22 (O[8], nand_13_out, nand_13_out);
endmodule

module And4 (
  input  [3:0] I,
  output O
);

  wire nand_1_out, nand_2_out, nand_3_out, nand_4_out, nand_5_out;

  nand nand_1 (nand_1_out, I[0], I[1]);
  nand nand_2 (nand_2_out, nand_1_out, nand_1_out);
  nand nand_3 (nand_3_out, nand_2_out, I[2]);
  nand nand_4 (nand_4_out, nand_3_out, nand_3_out);
  nand nand_5 (nand_5_out, nand_4_out, I[3]);
  nand nand_6 (O, nand_5_out, nand_5_out);
endmodule

module ControlDestination (
  input  OUTPUT_ENABLE,
  input  UPPER,
  input  LOWER,
  input  [2:0] S,
  output [36:0] O
);

  wire A_LOAD_HIGH_out, A_LOAD_LOW_out, B_LOAD_HIGH_out, B_LOAD_LOW_out, C_LOAD_HIGH_out, C_LOAD_LOW_out,
       D_LOAD_HIGH_out, D_LOAD_LOW_out, MARH_LOAD_HIGH_out, MARH_LOAD_LOW_out, MARL_LOAD_HIGH_out,
       MARL_LOAD_LOW_out, SP_LOAD_HIGH_out, SP_LOAD_LOW_out;
  wire [7:1] REG_DESTINATION_SELECT_o;

  Demux1To8S3 REG_DESTINATION_SELECT (
    .I(OUTPUT_ENABLE), .S(S), .O({REG_DESTINATION_SELECT_o[7:6], O[21], REG_DESTINATION_SELECT_o[4:1], O[9]}));
  nand A_LOAD_HIGH (A_LOAD_HIGH_out, UPPER, O[9]);
  nand nand_1 (O[8], A_LOAD_HIGH_out, A_LOAD_HIGH_out);
  nand A_LOAD_LOW (A_LOAD_LOW_out, LOWER, O[9]);
  nand B_LOAD_LOW (B_LOAD_LOW_out, REG_DESTINATION_SELECT_o[1], LOWER);
  nand B_LOAD_HIGH (B_LOAD_HIGH_out, REG_DESTINATION_SELECT_o[1], UPPER);
  nand C_LOAD_LOW (C_LOAD_LOW_out, REG_DESTINATION_SELECT_o[2], LOWER);
  nand C_LOAD_HIGH (C_LOAD_HIGH_out, REG_DESTINATION_SELECT_o[2], UPPER);
  nand D_LOAD_LOW (D_LOAD_LOW_out, REG_DESTINATION_SELECT_o[3], LOWER);
  nand D_LOAD_HIGH (D_LOAD_HIGH_out, REG_DESTINATION_SELECT_o[3], UPPER);
  nand SP_LOAD_LOW (SP_LOAD_LOW_out, REG_DESTINATION_SELECT_o[4], LOWER);
  nand SP_LOAD_HIGH (SP_LOAD_HIGH_out, REG_DESTINATION_SELECT_o[4], UPPER);
  nand MARL_LOAD_LOW (MARL_LOAD_LOW_out, REG_DESTINATION_SELECT_o[6], LOWER);
  nand MARL_LOAD_HIGH (MARL_LOAD_HIGH_out, REG_DESTINATION_SELECT_o[6], UPPER);
  nand MARH_LOAD_LOW (MARH_LOAD_LOW_out, REG_DESTINATION_SELECT_o[7], LOWER);
  nand MARH_LOAD_HIGH (MARH_LOAD_HIGH_out, REG_DESTINATION_SELECT_o[7], UPPER);
  nand nand_2 (O[7], A_LOAD_LOW_out, A_LOAD_LOW_out);
  nand nand_3 (O[11], B_LOAD_LOW_out, B_LOAD_LOW_out);
  nand nand_4 (O[12], B_LOAD_HIGH_out, B_LOAD_HIGH_out);
  nand nand_5 (O[14], C_LOAD_LOW_out, C_LOAD_LOW_out);
  nand nand_6 (O[15], C_LOAD_HIGH_out, C_LOAD_HIGH_out);
  nand nand_7 (O[17], D_LOAD_LOW_out, D_LOAD_LOW_out);
  nand nand_8 (O[18], D_LOAD_HIGH_out, D_LOAD_HIGH_out);
  nand nand_9 (O[24], SP_LOAD_LOW_out, SP_LOAD_LOW_out);
  nand nand_10 (O[25], SP_LOAD_HIGH_out, SP_LOAD_HIGH_out);
  nand nand_11 (O[31], MARL_LOAD_LOW_out, MARL_LOAD_LOW_out);
  nand nand_12 (O[32], MARL_LOAD_HIGH_out, MARL_LOAD_HIGH_out);
  nand nand_13 (O[33], MARH_LOAD_LOW_out, MARH_LOAD_LOW_out);
  nand nand_14 (O[34], MARH_LOAD_HIGH_out, MARH_LOAD_HIGH_out);
endmodule

module Or4 (
  input  [3:0] I,
  output O
);

  wire nand_1_out, nand_2_out, nand_3_out, nand_4_out, nand_5_out, nand_6_out, nand_7_out, nand_8_out;

  nand nand_1 (nand_1_out, I[0], I[0]);
  nand nand_2 (nand_2_out, I[1], I[1]);
  nand nand_3 (nand_3_out, nand_1_out, nand_2_out);
  nand nand_4 (nand_4_out, nand_3_out, nand_3_out);
  nand nand_5 (nand_5_out, I[2], I[2]);
  nand nand_6 (nand_6_out, nand_4_out, nand_5_out);
  nand nand_7 (nand_7_out, nand_6_out, nand_6_out);
  nand nand_8 (nand_8_out, I[3], I[3]);
  nand nand_9 (O, nand_7_out, nand_8_out);
endmodule

module ControlSource (
  input  OUTPUT_ENABLE,
  input  [2:0] S,
  output [36:0] O
);

  wire [7:7] demux1to8s3_1_o;

  Demux1To8S3 demux1to8s3_1 (
    .I(OUTPUT_ENABLE), .S(S), .O({demux1to8s3_1_o[7], O[22], O[23], O[26], O[19], O[16], O[13], O[6]}));
endmodule

module Or5 (
  input  [4:0] I,
  output O
);

  wire nand_1_out, nand_2_out, nand_3_out, nand_4_out, nand_5_out, nand_6_out, nand_7_out, nand_8_out,
       nand_9_out, nand_10_out, nand_11_out;

  nand nand_1 (nand_1_out, I[0], I[0]);
  nand nand_2 (nand_2_out, I[1], I[1]);
  nand nand_3 (nand_3_out, nand_1_out, nand_2_out);
  nand nand_4 (nand_4_out, nand_3_out, nand_3_out);
  nand nand_5 (nand_5_out, I[2], I[2]);
  nand nand_6 (nand_6_out, nand_4_out, nand_5_out);
  nand nand_7 (nand_7_out, nand_6_out, nand_6_out);
  nand nand_8 (nand_8_out, I[3], I[3]);
  nand nand_9 (nand_9_out, nand_7_out, nand_8_out);
  nand nand_10 (nand_10_out, nand_9_out, nand_9_out);
  nand nand_11 (nand_11_out, I[4], I[4]);
  nand nand_12 (O, nand_10_out, nand_11_out);
endmodule

module Or3 (
  input  [2:0] I,
  output O
);

  wire nand_1_out, nand_2_out, nand_3_out, nand_4_out, nand_5_out;

  nand nand_1 (nand_1_out, I[0], I[0]);
  nand nand_2 (nand_2_out, I[1], I[1]);
  nand nand_3 (nand_3_out, nand_1_out, nand_2_out);
  nand nand_4 (nand_4_out, nand_3_out, nand_3_out);
  nand nand_5 (nand_5_out, I[2], I[2]);
  nand nand_6 (O, nand_4_out, nand_5_out);
endmodule
